# Fritzing sketch Agrotech electric cycle sketch (saved by Fritzing 0.9.3b)

parts:
  Part1 = Arduino Nano (Rev3.0)
  Part2 = Soil Moisture Sensor
  U1 = RELAY [package=relay-t9a-2]
  VCC1 = Battery
  M1 = RioRand LM2596
  L1 = Solenoid

nets:
  GND: Part1.GND, Part2.GND, M1.Pin_4, L1.pin1
  N1: Part1.VIN, U1.COIL2
  N2: Part1.A4, U1.COIL1
  N3: Part1.A0, Part2.SIG
  3V3: Part1.3V3, Part2.VCC
  N4: U1.MAIN, VCC1.+
  N5: U1.NO, M1.Pin_1
  N6: VCC1.-, M1.Pin_2
  N7: M1.Pin_3, L1.pin2
